// Logisim project 8_bit_cpu.circ as structural Verilog: 3 circuits, main circuit Main
module FullAdder (
  input  in_1,
  input  in_2,
  input  in_3,
  output out_4,
  output out_5
);

  wire and_1_out, and_2_out, and_3_out;

  and and_1 (and_1_out, in_1, in_2);
  and and_2 (and_2_out, in_2, in_3);
  and and_3 (and_3_out, in_1, in_3);
  xor xor_1 (out_5, in_1, in_2, in_3);
  or or_1 (out_4, and_1_out, and_2_out, and_3_out);
endmodule

module Main (
  input  in_1,
  input  in_2,
  input  in_3,
  input  in_4,
  input  in_5,
  input  in_6,
  input  in_7,
  input  in_8,
  output out_9,
  output out_10,
  output out_11,
  output out_12,
  output out_13
);

  wire fulladder_2_out_4, fulladder_3_out_4, fulladder_4_out_4;

  FullAdder fulladder_1 (.in_1(in_1), .in_2(in_5), .in_3(fulladder_2_out_4), .out_5(out_10), .out_4(out_9));
  FullAdder fulladder_2 (.in_1(in_2), .in_2(in_6), .in_3(fulladder_3_out_4), .out_5(out_11), .out_4(fulladder_2_out_4));
  FullAdder fulladder_3 (.in_1(in_3), .in_2(in_7), .in_3(fulladder_4_out_4), .out_5(out_12), .out_4(fulladder_3_out_4));
  FullAdder fulladder_4 (.in_1(in_4), .in_2(in_8), .in_3(1'b0), .out_5(out_13), .out_4(fulladder_4_out_4));
endmodule

module Flipper (
  input  in_1,
  input  in_2,
  input  in_3,
  input  in_4,
  input  in_5,
  output out_6,
  output out_7,
  output out_8,
  output out_9
);

  xor xor_1 (out_6, in_1, in_5);
  xor xor_2 (out_7, in_2, in_5);
  xor xor_3 (out_8, in_3, in_5);
  xor xor_4 (out_9, in_4, in_5);
endmodule
